// Logisim project ControlUnit.circ as structural Verilog: 5 circuits, main circuit ControlUnit
module ControlUnit (
  input  [5:0] OpCode,
  input  [5:0] FunCode,
  input  Start,
  input  Clk,
  input  Rst,
  input  ZF,
  input  NF,
  input  RF
);

  wire and_1_out, and_2_out, demultiplexer_1_out0, demultiplexer_1_out1, EALU1, EB0, EB1, EBj, ED, EI, EJ,
       End, End0, END_q, Endj, EO2, EO_2, EO_2_t, EPC0, EPCj, ER1, ERb, ERs, EW1, IDLE_q, IOp, jr, mfhi,
       mflo, nop, or_1_out, or_2_out, or_5_out, PC1, PCnop, SPC, VOp;
  wire [1:0] OpType, SA0, SA1, SAj, SB0, SB1, SBj, SW1;
  wire [3:0] OpS, SALU0, SALU1, SALUj;

  OpDecoder opdecoder_1 (
    .OpCode(OpCode), .FunCode(FunCode),
    .Type__0_for_basic_type_R__and_1_for_special_R__2_for_type_I_and_3_for_type_J(OpType),
    .OpS__Selector_of_the_operation(OpS), .Valid__1_if_the_OC_and_FC_belong_to_a_valid_operation(VOp));
  Decoder #(.select(2), .disabled(0)) decoder_1 (.out0(ERb), .out1(ERs), .out2(EI), .out3(EJ), .sel(OpType), .en(ED));
  Decoder #(.select(2), .disabled(0)) decoder_2 (
    .out0(mfhi), .out1(mflo), .out2(nop), .out3(jr), .sel(OpS[1:0]), .en(EO_2_t));
  D_Flip_Flop IDLE (.clk(Clk), .D(or_1_out), .Q(IDLE_q), .preset(Rst));  // open: Qn, en, reset
  Demultiplexer #(.disabled(0), .enable("false")) demultiplexer_1 (
    .out0(demultiplexer_1_out0), .out1(demultiplexer_1_out1), .in(IDLE_q), .sel(Start));
  or or_1 (or_1_out, demultiplexer_1_out0, IOp);
  D_Flip_Flop u_END (.clk(Clk), .D(End), .Q(END_q), .reset(Rst));  // open: Qn, preset, en
  Comparator #(.width(2), .mode("unsigned")) comparator_1 (.a(2'b10), .b(OpS[3:2]), .gt(EO_2), .eq(EO2), .lt(EO_2_t));
  or or_2 (or_2_out, demultiplexer_1_out1, END_q);
  Demultiplexer #(.disabled(0), .enable("false")) demultiplexer_2 (.out0(IOp), .out1(ED), .in(or_2_out), .sel(VOp));
  or or_3 (End, End0, Endj);
  buf or_4 (SPC, PC1);  // OR_Gate
  D_Flip_Flop u_SPC (.clk(Clk), .D(SPC), .Q(PCnop), .reset(Rst));  // open: Qn, preset, en
  nop nop_1 (
    .Start(or_5_out), .Clk(Clk), .Rst(Rst), .SA(SA0), .SB(SB0), .EB(EB0), .SALU(SALU0), .EPC(EPC0), .End(End0));
  or or_5 (or_5_out, PCnop, and_1_out);
  and and_1 (and_1_out, ERb, nop);
  RbALUResult rbaluresult_1 (
    .Start(and_2_out), .Clk(Clk), .Rst(Rst), .SALU(OpS), .ER(ER1), .SA(SA1), .SB(SB1), .EB(EB1),
    .SALU_2(SALU1), .EALU(EALU1), .SW(SW1), .EW(EW1), .End(PC1));
  and and_2 (and_2_out, EO_2, ERb);
  j j_1 (.Start(EJ), .Clk(Clk), .Rst(Rst), .SA(SAj), .SB(SBj), .EB(EBj), .SALU(SALUj), .EPC(EPCj), .End(Endj));

  // Other names for the same wires on the sheet: FC[5:0] = FunCode; OC[5:0] = OpCode; SO[1:0] = OpS[1:0]; St = Start

  // Notes on the sheet:
  //   Input
  //   Output
  //   Initial Circuit
  //   Selector Decoder
  //   End Instruction
  //   Save PC Instruction
  //   Machines
  //   Cambiar numeros
endmodule

module OpDecoder (
  input  [5:0] OpCode,
  input  [5:0] FunCode,
  output [1:0] Type__0_for_basic_type_R__and_1_for_special_R__2_for_type_I_and_3_for_type_J,
  output [3:0] OpS__Selector_of_the_operation,
  output Valid__1_if_the_OC_and_FC_belong_to_a_valid_operation
);

  wire and_1_out, comparator_5_eq, comparator_6_eq, comparator_7_eq, comparator_8_eq, comparator_9_eq,
       comparator_10_eq, comparator_11_eq, comparator_12_eq, comparator_13_eq, comparator_14_eq,
       comparator_15_eq, comparator_16_eq, comparator_17_eq, comparator_18_eq, comparator_19_eq,
       comparator_20_eq, I, J, Rb, Rs, Rs0, Rs1, VRb;
  wire [3:0] OpSI, OpSJ, OpSRb, OpSRs;

  Comparator #(.width(6)) comparator_1 (.a(OpCode), .b(6'b000010), .eq(J));  // open: gt, lt
  Comparator #(.width(6)) comparator_2 (.a(OpCode), .b({6{1'b0}}), .eq(Rb));  // open: gt, lt
  Comparator #(.width(6)) comparator_3 (.a(OpCode), .b(6'b111000), .eq(Rs0));  // open: gt, lt
  Comparator #(.width(6)) comparator_4 (.a(OpCode), .b({6{1'b1}}), .eq(Rs1));  // open: gt, lt
  or or_1 (Rs, Rs0, Rs1);
  nor nor_1 (I, Rb, Rs, J);
  Priority_Encoder #(.select(2)) priority_encoder_1 (
    .in0(Rb), .in1(Rs), .in2(I), .in3(J),
    .out(Type__0_for_basic_type_R__and_1_for_special_R__2_for_type_I_and_3_for_type_J));  // open: gs, en_out, en_in
  Comparator #(.width(6)) comparator_5 (.a(FunCode), .b(6'b100000), .eq(comparator_5_eq));  // open: gt, lt
  Comparator #(.width(6)) comparator_6 (.a(FunCode), .b(6'b100010), .eq(comparator_6_eq));  // open: gt, lt
  Comparator #(.width(6)) comparator_7 (.a(FunCode), .b(6'b100100), .eq(comparator_7_eq));  // open: gt, lt
  Comparator #(.width(6)) comparator_8 (.a(FunCode), .b(6'b100101), .eq(comparator_8_eq));  // open: gt, lt
  Comparator #(.width(6)) comparator_9 (.a(FunCode), .b(6'b100111), .eq(comparator_9_eq));  // open: gt, lt
  Comparator #(.width(6)) comparator_10 (.a(FunCode), .b(6'b101000), .eq(comparator_10_eq));  // open: gt, lt
  Comparator #(.width(6)) comparator_11 (.a(FunCode), .b(6'b101010), .eq(comparator_11_eq));  // open: gt, lt
  Comparator #(.width(6)) comparator_12 (.a(FunCode), .b(6'b101011), .eq(comparator_12_eq));  // open: gt, lt
  Comparator #(.width(6)) comparator_13 (.a(FunCode), .b(6'b011000), .eq(comparator_13_eq));  // open: gt, lt
  Comparator #(.width(6)) comparator_14 (.a(FunCode), .b(6'b011001), .eq(comparator_14_eq));  // open: gt, lt
  Comparator #(.width(6)) comparator_15 (.a(FunCode), .b(6'b011010), .eq(comparator_15_eq));  // open: gt, lt
  Comparator #(.width(6)) comparator_16 (.a(FunCode), .b(6'b011011), .eq(comparator_16_eq));  // open: gt, lt
  Comparator #(.width(6)) comparator_17 (.a(FunCode), .b(6'b010000), .eq(comparator_17_eq));  // open: gt, lt
  Comparator #(.width(6)) comparator_18 (.a(FunCode), .b(6'b010010), .eq(comparator_18_eq));  // open: gt, lt
  Comparator #(.width(6)) comparator_19 (.a(FunCode), .b({6{1'b0}}), .eq(comparator_19_eq));  // open: gt, lt
  Comparator #(.width(6)) comparator_20 (.a(FunCode), .b(6'b001000), .eq(comparator_20_eq));  // open: gt, lt
  Priority_Encoder #(.select(4), .disabled(0)) priority_encoder_2 (
    .in0(comparator_5_eq), .in1(comparator_6_eq), .in2(comparator_7_eq), .in3(comparator_8_eq),
    .in4(comparator_9_eq), .in5(comparator_10_eq), .in6(comparator_11_eq), .in7(comparator_12_eq),
    .in8(comparator_13_eq), .in9(comparator_14_eq), .in10(comparator_15_eq), .in11(comparator_16_eq),
    .in12(comparator_17_eq), .in13(comparator_18_eq), .in14(comparator_19_eq), .in15(comparator_20_eq),
    .out(OpSRb), .gs(VRb), .en_in(Rb));  // open: en_out
  and and_1 (and_1_out, Rb, VRb);
  Pull_Resistor pull_resistor_1 (.node(OpSRb));
  Pull_Resistor pull_resistor_2 (.node(OpSRs));
  Pull_Resistor pull_resistor_3 (.node(OpSI));
  Pull_Resistor pull_resistor_4 (.node(OpSJ));
  or or_2 (Valid__1_if_the_OC_and_FC_belong_to_a_valid_operation, J, and_1_out);
  assign OpS__Selector_of_the_operation = OpSRb | OpSRs | OpSI | OpSJ;  // OR_Gate or_3, 4 bits wide

  // Other names for the same wires on the sheet: FC[5:0] = FunCode; OC[5:0] = OpCode;
  //   OpS[3:0] = OpS__Selector_of_the_operation;
  //   Type[1:0] = Type__0_for_basic_type_R__and_1_for_special_R__2_for_type_I_and_3_for_type_J;
  //   Valid = Valid__1_if_the_OC_and_FC_belong_to_a_valid_operation

  // Notes on the sheet:
  //   Agregar encoder de Rs y I 
  //   Agregar las de Rs y I
endmodule

module RbALUResult (
  input  Start,
  input  Clk,
  input  Rst,
  input  [3:0] SALU,
  output ER,
  output [1:0] SA,
  output [1:0] SB,
  output EB,
  output [3:0] SALU_2,
  output EALU,
  output [1:0] SW,
  output EW,
  output End
);

  Multiplexer #(.width(2), .disabled(0), .enable("false")) multiplexer_1 (
    .in0(2'b00), .in1(2'b01), .out(SA), .sel(Start));
  Multiplexer #(.width(2), .disabled(0), .enable("false")) multiplexer_2 (
    .in0(2'b00), .in1(2'b01), .out(SB), .sel(Start));
  Multiplexer #(.width(4), .disabled(0), .enable("false")) multiplexer_3 (
    .in0(4'b0000), .in1(SALU), .out(SALU_2), .sel(Start));

  assign EALU = Start;
  assign EB = Start;
  assign End = Start;
  assign ER = Start;
  assign EW = Start;
  assign SW = 2'b00;

  // Other names for the same wires on the sheet: St = Start

  // Notes on the sheet:
  //   Input
  //   Ground
  //   Output
endmodule

module nop (
  input  Start,
  input  Clk,
  input  Rst,
  output [1:0] SA,
  output [1:0] SB,
  output EB,
  output [3:0] SALU,
  output EPC,
  output End
);


  assign EB = Start;
  assign End = Start;
  assign EPC = Start;
  assign SA = 2'b00;
  assign SALU = 4'b0000;
  assign SB = 2'b00;

  // Other names for the same wires on the sheet: St = Start

  // Notes on the sheet:
  //   Input
  //   Ground
  //   Output
endmodule

module j (
  input  Start,
  input  Clk,
  input  Rst,
  output [1:0] SA,
  output [1:0] SB,
  output EB,
  output [3:0] SALU,
  output EPC,
  output End
);

  Multiplexer #(.width(2), .disabled(0), .enable("false")) multiplexer_1 (
    .in0(2'b00), .in1(2'b10), .out(SA), .sel(Start));

  assign EB = 1'b0;
  assign End = Start;
  assign EPC = Start;
  assign SALU = 4'b0000;
  assign SB = 2'b00;

  // Other names for the same wires on the sheet: St = Start

  // Notes on the sheet:
  //   Input
  //   Ground
  //   Output
endmodule
